# Fritzing sketch Scehmatics (saved by Fritzing 0.9.3b)

parts:
  Raspberry_Pi1 = Raspberry Pi B+
  M1 = NEO-6M GPS Module [part_number=GY-GPS6MV2]

nets:
  N1: Raspberry_Pi1.GPIO15, M1.Tx
  N2: Raspberry_Pi1.GPIO14, M1.Rx
  GND: Raspberry_Pi1.GND, M1.GND
  5V: Raspberry_Pi1.5V, M1.Vcc

custom parts:
  NEO-6M GPS Module: GY-GPS6MV2 NEO-6M GPS Module Module based on U-blox NEO-6M GPS engine, incorporating regulator for 3.3-5V DC input, MS621FE-compatible rechargeable battery for backup and EEPROM for storing configuration settings. Links: NEO-6 series product information page NEO-6 Datasheet
